# Fritzing sketch step1_backup_project (saved by Fritzing 0.9.3b)
breadboards: 1

parts:
  Part1 = Arduino Micro (Rev3)
  S1 = Momentary Switch [package=ksa_sealed_tac_switch]
  S2 = Momentary Switch [package=ksa_sealed_tac_switch]
  U1 = POT [package=3362u]

nets:
  N1: Part1.GND, S1.2, S2.2, U1.E
  N2: Part1.D6_PWM/A7, S1.4
  N3: Part1.D7, S2.4
  N4: Part1.5V, U1.A
  N5: Part1.A5, U1.S

notes:
  Arduino Micro
  +++++++++++
  Button1 -> 6 pin PC6
  Button2 -> 7 pin PD7
  Sensor -> A5
  +5
  GND
